# Fritzing sketch thermalcoupler (saved by Fritzing 0.9.3b)
breadboards: 1

parts:
  Part1 = Arduino Uno (Rev3) - ICSP
  Part3 = SparkFun_Beefcake_Relay_Control_Kit
  SparkFun_Serial_LCD_Kit1 = Serial LCD Kit [part_number=LCD-10097 package="DIP (Dual Inline) [THT]"]
  PART1 = SparkFun MAX31855K Thermocouple Breakout [part_number=SEN-13266]  # not connected
  U1 = POT [package=pot_mammoth]

nets:
  N1: Part1.A0, U1.A
  N2: Part1.D2, SparkFun_Serial_LCD_Kit1.RX
  N3: Part1.D4, Part3.RELAY
  5V: Part1.5V, Part3.VCC, SparkFun_Serial_LCD_Kit1.5V, U1.E
  GND: Part1.GND, Part3.GND, SparkFun_Serial_LCD_Kit1.GND, U1.S

custom parts:
  Serial LCD Kit: Calling this the "Serial Enabled LCD Kit" doesn't do justice to how cool it actually is. After you've assembled this all-PTH kit, you'll be left with a fully Arduino-compatible development board that just happens to have a white on black 16x2 display built-in. Turns out the ATMega328 is pretty far over-spec for just controlling a parallel LCD so there's a lot of horsepower left over to do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
  SparkFun MAX31855K Thermocouple Breakout: The MAX31855K IC takes a standard k-type thermocouple in one end, digitizes the temperature measured and sends that data out the other end via SPI. For more information, please visit www.sparkfun.com
